# Fritzing sketch circuit (saved by Fritzing 0.9.3b)
breadboards: 1

parts:
  S1 = Pushbutton [package="[THT]"]
  VCC1 = 4 x AAA Battery Mount  # not connected
  R1 = Resistor [tolerance=±5% resistance=220 package="2010 [SMD]"]

nets:
  N1: S1.Pin_1, S1.Pin_2, R1.Pin_1
  N2: S1.Pin_3, S1.Pin_4
